# Fritzing sketch Conexion DS18B20_sumergible (saved by Fritzing 0.9.3b)

parts:
  Part1 = Arduino Uno (Rev3)
  DS1 = DS18B20 1-Wire Temperature Sensor Probe Cable
  R1 = Resistor [tolerance=±5% resistance=4.7k package=THT]

nets:
  N1: Part1.D2, DS1.shield, R1.Pin_0
  5V: Part1.5V, DS1.VDD, R1.Pin_1
  GND: Part1.GND, DS1.GND
